// Logisim project stack_logical_easy.circ as structural Verilog: 2 circuits, main circuit main
module main (
  input  CLK,
  input  RESET,
  input  [1:0] COMMAND,
  input  [2:0] INDEX,
  input  [3:0] IDATA,
  output [3:0] ODATA
);

  stack stack_1 (.CLK(CLK), .RESET(RESET), .COMMAND(COMMAND), .INDEX(INDEX), .IDATA(IDATA), .ODATA(ODATA));
endmodule

module stack (
  input  CLK,
  input  RESET,
  input  [1:0] COMMAND,
  input  [2:0] INDEX,
  input  [3:0] IDATA,
  output [3:0] ODATA
);


  // Notes on the sheet:
  //   your circuit must be here
endmodule
