// Logisim project stack_logical_normal.circ as structural Verilog: 27 circuits, main circuit main
module main (
  input  CLK,
  input  RESET,
  input  [1:0] COMMAND,
  input  [2:0] INDEX,
  input  [3:0] IO_DATA_in,
  output [3:0] IO_DATA_out
);

  stack stack_1 (
    .CLK(CLK), .RESET(RESET), .COMMAND(COMMAND), .INDEX(INDEX), .IO_DATA_in(IO_DATA_in),
    .IO_DATA_out(IO_DATA_out));
endmodule

module stack (
  input  CLK,
  input  RESET,
  input  [1:0] COMMAND,
  input  [2:0] INDEX,
  input  [3:0] IO_DATA_in,
  output [3:0] IO_DATA_out
);

  wire decoder_2_to_4_1_q0, decoder_2_to_4_1_q1, decoder_2_to_4_1_q2, decoder_2_to_4_1_q3, or_1_out,
       or_2_out, por_1_out, u_to_0_1_o, u_to_0_2_o;
  wire [3:0] byte_u_to_0_1_o, dddd_and_a_1_q, dddd_and_a_2_q, head_1_index, or_3_out, sub_mod_5_1_s;
  wire [3:3] undriven;

  U_to_0 u_to_0_1 (.I(CLK), .O(u_to_0_1_o));
  U_to_0 u_to_0_2 (.I(RESET), .O(u_to_0_2_o));
  // NoConnect on decoder_2_to_4_1_q0
  decoder_2_to_4 decoder_2_to_4_1 (
    .i0(COMMAND[0]), .i1(COMMAND[1]), .Q0(decoder_2_to_4_1_q0), .Q1(decoder_2_to_4_1_q1),
    .Q2(decoder_2_to_4_1_q2), .Q3(decoder_2_to_4_1_q3));
  byte_U_to_0 byte_u_to_0_1 (.I({undriven[3], INDEX}), .O(byte_u_to_0_1_o));
  or or_1 (or_1_out, u_to_0_2_o, por_1_out);
  POR por_1 (.out(por_1_out));
  DDDD_AND_A dddd_and_a_1 (.D(4'b0100), .A(decoder_2_to_4_1_q2), .Q(dddd_and_a_1_q));
  DDDD_AND_A dddd_and_a_2 (.D(byte_u_to_0_1_o), .A(decoder_2_to_4_1_q3), .Q(dddd_and_a_2_q));
  or or_2 (or_2_out, decoder_2_to_4_1_q3, decoder_2_to_4_1_q2);
  assign or_3_out = dddd_and_a_1_q | dddd_and_a_2_q;  // OR_Gate or_3, 4 bits wide
  // Probe on head_1_index
  HEAD head_1 (
    .INCR(decoder_2_to_4_1_q1), .DECR(decoder_2_to_4_1_q2), .CLK(u_to_0_1_o), .RESET(or_1_out),
    .INDEX(head_1_index));
  SUB_mod_5 sub_mod_5_1 (.X(head_1_index), .Y(or_3_out), .S(sub_mod_5_1_s));
  MEMORY memory_1 (
    .GET(or_2_out), .SET(decoder_2_to_4_1_q1), .INDEX(sub_mod_5_1_s), .IDATA(IO_DATA_in), .CLK(u_to_0_1_o),
    .RESET(or_1_out), .ODATA(IO_DATA_in));

  assign IO_DATA_out = IO_DATA_in;

  // Notes on the sheet:
  //   00 - nop
  //   01 - push
  //   10 - pop
  //   11 - get
  //   get
  //   pop
  //   push
endmodule

module HEAD (
  input  INCR,
  input  DECR,
  input  CLK,
  input  RESET,
  output [3:0] INDEX
);

  wire and_1_out, not_1_out, or_1_out, or_3_out;
  wire [3:0] dddd_and_a_1_q, dddd_and_a_2_q, dddd_and_a_3_q, dddd_and_a_4_q, decrement_mod_5_1_odata,
       increment_mod_5_1_odata, or_2_out, or_4_out;

  DDDD_AND_A dddd_and_a_1 (.D(increment_mod_5_1_odata), .A(INCR), .Q(dddd_and_a_1_q));
  DDDD_AND_A dddd_and_a_2 (.D(decrement_mod_5_1_odata), .A(DECR), .Q(dddd_and_a_2_q));
  or or_1 (or_1_out, INCR, DECR);
  assign or_2_out = dddd_and_a_1_q | dddd_and_a_2_q;  // OR_Gate or_2, 4 bits wide
  not not_1 (not_1_out, RESET);
  and and_1 (and_1_out, or_1_out, CLK);
  DDDD_AND_A dddd_and_a_3 (.D(or_2_out), .A(not_1_out), .Q(dddd_and_a_3_q));
  DDDD_AND_A dddd_and_a_4 (.D(4'b0100), .A(RESET), .Q(dddd_and_a_4_q));
  or or_3 (or_3_out, and_1_out, RESET);
  // Probe on or_4_out
  assign or_4_out = dddd_and_a_3_q | dddd_and_a_4_q;  // OR_Gate or_4, 4 bits wide
  // Probe on INDEX
  quad_memory_back quad_memory_back_1 (.IDATA(or_4_out), .SET(or_3_out), .ODATA(INDEX));
  // Probe on increment_mod_5_1_odata
  increment_mod_5 increment_mod_5_1 (.IDATA(INDEX), .ODATA(increment_mod_5_1_odata));
  decrement_mod_5 decrement_mod_5_1 (.IDATA(INDEX), .ODATA(decrement_mod_5_1_odata));
  // Probe on decrement_mod_5_1_odata
endmodule

module MEMORY (
  input  GET,
  input  SET,
  input  [3:0] INDEX,
  input  [3:0] IDATA,
  input  CLK,
  input  RESET,
  output [3:0] ODATA
);

  wire and_1_out, and_2_out, and_3_out, and_4_out, and_5_out, and_6_out, demux_3_to_8_1_i0,
       demux_3_to_8_1_i1, demux_3_to_8_1_i2, demux_3_to_8_1_i3, demux_3_to_8_1_i4, demux_3_to_8_2_i0,
       demux_3_to_8_2_i1, demux_3_to_8_2_i2, demux_3_to_8_2_i3, demux_3_to_8_2_i4, not_1_out, not_2_out,
       not_3_out, not_4_out, not_5_out, or_1_out, or_2_out, or_3_out, or_4_out, or_5_out, or_6_out, por_1_out;
  wire [3:0] dddd_and_a_1_q, dddd_and_a_2_q, dddd_and_a_3_q, dddd_and_a_4_q, dddd_and_a_5_q, dddd_and_a_6_q,
       dddd_and_a_7_q, dddd_and_a_8_q, dddd_and_a_9_q, dddd_and_a_10_q, or_7_out, or_8_out, or_9_out,
       or_10_out, quad_memory_1_odata, quad_memory_2_odata, quad_memory_3_odata, quad_memory_4_odata,
       quad_memory_5_odata;

  DEMUX_3_to_8 demux_3_to_8_1 (
    .S(INDEX), .D(SET), .i0(demux_3_to_8_1_i0), .i1(demux_3_to_8_1_i1), .i2(demux_3_to_8_1_i2),
    .i3(demux_3_to_8_1_i3), .i4(demux_3_to_8_1_i4));  // open: i5, i6, i7
  POR #(.PorHighDuration(1)) por_1 (.out(por_1_out));
  not not_1 (not_1_out, or_1_out);
  and and_1 (and_1_out, demux_3_to_8_1_i0, CLK);
  not not_2 (not_2_out, or_1_out);
  and and_2 (and_2_out, demux_3_to_8_1_i1, CLK);
  not not_3 (not_3_out, or_1_out);
  and and_3 (and_3_out, demux_3_to_8_1_i2, CLK);
  not not_4 (not_4_out, or_1_out);
  and and_4 (and_4_out, demux_3_to_8_1_i3, CLK);
  not not_5 (not_5_out, or_1_out);
  and and_5 (and_5_out, demux_3_to_8_1_i4, CLK);
  or or_1 (or_1_out, RESET, por_1_out);
  DDDD_AND_A dddd_and_a_1 (.D(IDATA), .A(not_1_out), .Q(dddd_and_a_1_q));
  or or_2 (or_2_out, or_1_out, and_1_out);
  DDDD_AND_A dddd_and_a_2 (.D(IDATA), .A(not_2_out), .Q(dddd_and_a_2_q));
  or or_3 (or_3_out, or_1_out, and_2_out);
  DDDD_AND_A dddd_and_a_3 (.D(IDATA), .A(not_3_out), .Q(dddd_and_a_3_q));
  or or_4 (or_4_out, or_1_out, and_3_out);
  DDDD_AND_A dddd_and_a_4 (.D(IDATA), .A(not_4_out), .Q(dddd_and_a_4_q));
  or or_5 (or_5_out, or_1_out, and_4_out);
  DDDD_AND_A dddd_and_a_5 (.D(IDATA), .A(not_5_out), .Q(dddd_and_a_5_q));
  or or_6 (or_6_out, or_1_out, and_5_out);
  DEMUX_3_to_8 demux_3_to_8_2 (
    .S(INDEX), .D(GET), .i0(demux_3_to_8_2_i0), .i1(demux_3_to_8_2_i1), .i2(demux_3_to_8_2_i2),
    .i3(demux_3_to_8_2_i3), .i4(demux_3_to_8_2_i4));  // open: i5, i6, i7
  // Probe on quad_memory_1_odata
  quad_memory quad_memory_1 (.IDATA(dddd_and_a_1_q), .SET(or_2_out), .ODATA(quad_memory_1_odata));
  // Probe on quad_memory_2_odata
  quad_memory quad_memory_2 (.IDATA(dddd_and_a_2_q), .SET(or_3_out), .ODATA(quad_memory_2_odata));
  // Probe on quad_memory_3_odata
  quad_memory quad_memory_3 (.IDATA(dddd_and_a_3_q), .SET(or_4_out), .ODATA(quad_memory_3_odata));
  // Probe on quad_memory_4_odata
  quad_memory quad_memory_4 (.IDATA(dddd_and_a_4_q), .SET(or_5_out), .ODATA(quad_memory_4_odata));
  // Probe on quad_memory_5_odata
  quad_memory quad_memory_5 (.IDATA(dddd_and_a_5_q), .SET(or_6_out), .ODATA(quad_memory_5_odata));
  DDDD_AND_A dddd_and_a_6 (.D(quad_memory_1_odata), .A(demux_3_to_8_2_i0), .Q(dddd_and_a_6_q));
  assign or_7_out = dddd_and_a_6_q | dddd_and_a_7_q;  // OR_Gate or_7, 4 bits wide
  DDDD_AND_A dddd_and_a_7 (.D(quad_memory_2_odata), .A(demux_3_to_8_2_i1), .Q(dddd_and_a_7_q));
  DDDD_AND_A dddd_and_a_8 (.D(quad_memory_3_odata), .A(demux_3_to_8_2_i2), .Q(dddd_and_a_8_q));
  assign or_8_out = dddd_and_a_8_q | dddd_and_a_9_q;  // OR_Gate or_8, 4 bits wide
  DDDD_AND_A dddd_and_a_9 (.D(quad_memory_4_odata), .A(demux_3_to_8_2_i3), .Q(dddd_and_a_9_q));
  DDDD_AND_A dddd_and_a_10 (.D(quad_memory_5_odata), .A(demux_3_to_8_2_i4), .Q(dddd_and_a_10_q));
  assign or_9_out = or_7_out | or_8_out;  // OR_Gate or_9, 4 bits wide
  assign or_10_out = or_9_out | dddd_and_a_10_q;  // OR_Gate or_10, 4 bits wide
  and and_6 (and_6_out, GET, CLK);
  DATA_if_F_else_UUUU data_if_f_else_uuuu_1 (.F(and_6_out), .DATA(or_10_out), .ODATA(ODATA));
endmodule

module increment_mod_5 (
  input  [3:0] IDATA,
  output [3:0] ODATA
);

  wire and_1_out, not_1_out;
  wire [3:0] dddd_and_a_1_q, dddd_and_a_2_q, increment_1_odata;

  // NoConnect on IDATA[3]
  and and_1 (and_1_out, increment_1_odata[0], ~increment_1_odata[1], increment_1_odata[2]);  // AND_Gate
  increment increment_1 (.IDATA({1'b0, IDATA[2:0]}), .ODATA(increment_1_odata));
  not not_1 (not_1_out, and_1_out);
  DDDD_AND_A dddd_and_a_1 (.D(increment_1_odata), .A(not_1_out), .Q(dddd_and_a_1_q));
  assign ODATA = dddd_and_a_1_q | dddd_and_a_2_q;  // OR_Gate or_1, 4 bits wide
  DDDD_AND_A dddd_and_a_2 (.D(4'b0000), .A(and_1_out), .Q(dddd_and_a_2_q));

  // Notes on the sheet:
  //   // избавляемся от старшего бита
  //    (на всякий случай...)
  //   if (DATA == 101) DATA = 0;
endmodule

module decrement_mod_5 (
  input  [3:0] IDATA,
  output [3:0] ODATA
);

  wire and_1_out, not_1_out;
  wire [3:0] dddd_and_a_1_q, dddd_and_a_2_q, decrement_1_odata;

  // NoConnect on IDATA[3]
  and and_1 (and_1_out, decrement_1_odata[0], decrement_1_odata[1], decrement_1_odata[2]);
  decrement decrement_1 (.IDATA({1'b0, IDATA[2:0]}), .ODATA(decrement_1_odata));
  not not_1 (not_1_out, and_1_out);
  DDDD_AND_A dddd_and_a_1 (.D(decrement_1_odata), .A(not_1_out), .Q(dddd_and_a_1_q));
  assign ODATA = dddd_and_a_1_q | dddd_and_a_2_q;  // OR_Gate or_1, 4 bits wide
  DDDD_AND_A dddd_and_a_2 (.D(4'b0100), .A(and_1_out), .Q(dddd_and_a_2_q));

  // Notes on the sheet:
  //   // избавляемся от старшего бита
  //    (на всякий случай...)
  //   if (DATA == 0) DATA = 100;
endmodule

module increment (
  input  [3:0] IDATA,
  output [3:0] ODATA
);

  wire sum_4_bits_1_c;

  SUM_4_bits sum_4_bits_1 (.X(IDATA), .Y(4'b0001), .S(ODATA), .C(sum_4_bits_1_c));
  // NoConnect on sum_4_bits_1_c

  // Notes on the sheet:
  //   // прибавим 1
endmodule

module decrement (
  input  [3:0] IDATA,
  output [3:0] ODATA
);

  wire sum_4_bits_1_c;

  SUM_4_bits sum_4_bits_1 (.X(IDATA), .Y(4'b1111), .S(ODATA), .C(sum_4_bits_1_c));
  // NoConnect on sum_4_bits_1_c

  // Notes on the sheet:
  //   // прибавим 15 (-1)
endmodule

module SUB_mod_5 (
  input  [3:0] X,
  input  [3:0] Y,
  output [3:0] S
);

  wire [3:0] sub_4_bits_1_s;

  SUB_4_bits sub_4_bits_1 (.X(X), .Y(Y), .S(sub_4_bits_1_s));
  mod_5 mod_5_1 (.X(sub_4_bits_1_s), .X_mod_5(S));
endmodule

module mod_5 (
  input  [3:0] X,
  output [3:0] X_mod_5
);

  wire n0_out, n1_out, n2_out, n3_out, n4_out, n5_out, n6_out, n7_out, n8_out, n9_out, n10_out, n11_out,
       n12_out, n13_out, n14_out, n15_out;
  wire [3:0] dddd_and_a_1_q, dddd_and_a_2_q, dddd_and_a_3_q, dddd_and_a_4_q, dddd_and_a_5_q, dddd_and_a_6_q,
       dddd_and_a_7_q, dddd_and_a_8_q, dddd_and_a_9_q, dddd_and_a_10_q, dddd_and_a_11_q, dddd_and_a_12_q,
       dddd_and_a_13_q, dddd_and_a_14_q, dddd_and_a_15_q, dddd_and_a_16_q, or_1_out, or_2_out, or_3_out,
       or_4_out, or_5_out, or_6_out, or_7_out, or_8_out, or_9_out, or_10_out, or_11_out, or_12_out,
       or_13_out, or_14_out;

  and n0 (n0_out, ~X[0], ~X[1], ~X[2], ~X[3]);  // AND_Gate
  and n1 (n1_out, X[0], ~X[1], ~X[2], ~X[3]);  // AND_Gate
  and n2 (n2_out, ~X[0], X[1], ~X[2], ~X[3]);  // AND_Gate
  and n3 (n3_out, X[0], X[1], ~X[2], ~X[3]);  // AND_Gate
  and n4 (n4_out, ~X[0], ~X[1], X[2], ~X[3]);  // AND_Gate
  and n5 (n5_out, X[0], ~X[1], X[2], ~X[3]);  // AND_Gate
  and n6 (n6_out, ~X[0], X[1], X[2], ~X[3]);  // AND_Gate
  and n7 (n7_out, X[0], X[1], X[2], ~X[3]);  // AND_Gate
  and n8 (n8_out, ~X[0], ~X[1], ~X[2], X[3]);  // AND_Gate
  and n9 (n9_out, X[0], ~X[1], ~X[2], X[3]);  // AND_Gate
  and n10 (n10_out, ~X[0], X[1], ~X[2], X[3]);  // AND_Gate
  and n11 (n11_out, X[0], X[1], ~X[2], X[3]);  // AND_Gate
  and n12 (n12_out, ~X[0], ~X[1], X[2], X[3]);  // AND_Gate
  and n13 (n13_out, X[0], ~X[1], X[2], X[3]);  // AND_Gate
  and n14 (n14_out, ~X[0], X[1], X[2], X[3]);  // AND_Gate
  and n15 (n15_out, X[0], X[1], X[2], X[3]);
  DDDD_AND_A dddd_and_a_1 (.D(4'b0000), .A(n0_out), .Q(dddd_and_a_1_q));
  DDDD_AND_A dddd_and_a_2 (.D(4'b0001), .A(n1_out), .Q(dddd_and_a_2_q));
  DDDD_AND_A dddd_and_a_3 (.D(4'b0010), .A(n2_out), .Q(dddd_and_a_3_q));
  DDDD_AND_A dddd_and_a_4 (.D(4'b0011), .A(n3_out), .Q(dddd_and_a_4_q));
  DDDD_AND_A dddd_and_a_5 (.D(4'b0100), .A(n4_out), .Q(dddd_and_a_5_q));
  DDDD_AND_A dddd_and_a_6 (.D(4'b0000), .A(n5_out), .Q(dddd_and_a_6_q));
  DDDD_AND_A dddd_and_a_7 (.D(4'b0001), .A(n6_out), .Q(dddd_and_a_7_q));
  DDDD_AND_A dddd_and_a_8 (.D(4'b0001), .A(n7_out), .Q(dddd_and_a_8_q));
  DDDD_AND_A dddd_and_a_9 (.D(4'b0010), .A(n8_out), .Q(dddd_and_a_9_q));
  DDDD_AND_A dddd_and_a_10 (.D(4'b0011), .A(n9_out), .Q(dddd_and_a_10_q));
  DDDD_AND_A dddd_and_a_11 (.D(4'b0100), .A(n10_out), .Q(dddd_and_a_11_q));
  DDDD_AND_A dddd_and_a_12 (.D(4'b0000), .A(n11_out), .Q(dddd_and_a_12_q));
  DDDD_AND_A dddd_and_a_13 (.D(4'b0001), .A(n12_out), .Q(dddd_and_a_13_q));
  DDDD_AND_A dddd_and_a_14 (.D(4'b0010), .A(n13_out), .Q(dddd_and_a_14_q));
  DDDD_AND_A dddd_and_a_15 (.D(4'b0011), .A(n14_out), .Q(dddd_and_a_15_q));
  DDDD_AND_A dddd_and_a_16 (.D(4'b0100), .A(n15_out), .Q(dddd_and_a_16_q));
  assign or_1_out = dddd_and_a_1_q | dddd_and_a_2_q;  // OR_Gate or_1, 4 bits wide
  assign or_2_out = or_1_out | or_3_out;  // OR_Gate or_2, 4 bits wide
  assign or_3_out = dddd_and_a_3_q | dddd_and_a_4_q;  // OR_Gate or_3, 4 bits wide
  assign or_4_out = dddd_and_a_5_q | dddd_and_a_6_q;  // OR_Gate or_4, 4 bits wide
  assign or_5_out = or_4_out | or_6_out;  // OR_Gate or_5, 4 bits wide
  assign or_6_out = dddd_and_a_7_q | dddd_and_a_8_q;  // OR_Gate or_6, 4 bits wide
  assign or_7_out = dddd_and_a_9_q | dddd_and_a_10_q;  // OR_Gate or_7, 4 bits wide
  assign or_8_out = or_7_out | or_9_out;  // OR_Gate or_8, 4 bits wide
  assign or_9_out = dddd_and_a_11_q | dddd_and_a_12_q;  // OR_Gate or_9, 4 bits wide
  assign or_10_out = dddd_and_a_13_q | dddd_and_a_14_q;  // OR_Gate or_10, 4 bits wide
  assign or_11_out = or_10_out | or_12_out;  // OR_Gate or_11, 4 bits wide
  assign or_12_out = dddd_and_a_15_q | dddd_and_a_16_q;  // OR_Gate or_12, 4 bits wide
  assign or_13_out = or_2_out | or_5_out;  // OR_Gate or_13, 4 bits wide
  assign or_14_out = or_8_out | or_11_out;  // OR_Gate or_14, 4 bits wide
  assign X_mod_5 = or_13_out | or_14_out;  // OR_Gate or_15, 4 bits wide

  // Notes on the sheet:
  //   Извините.
endmodule

module SUB_4_bits (
  input  [3:0] X,
  input  [3:0] Y,
  output [3:0] S
);

  wire sum_4_bits_1_c, sum_4_bits_2_c;
  wire [3:0] not_1_out, sum_4_bits_1_s;

  assign not_1_out = ~Y;  // NOT_Gate not_1, 4 bits wide
  SUM_4_bits sum_4_bits_1 (.X(X), .Y(not_1_out), .S(sum_4_bits_1_s), .C(sum_4_bits_1_c));
  // NoConnect on sum_4_bits_1_c
  SUM_4_bits sum_4_bits_2 (.X(sum_4_bits_1_s), .Y(4'b0001), .S(S), .C(sum_4_bits_2_c));
  // NoConnect on sum_4_bits_2_c
endmodule

module SUM_4_bits (
  input  [3:0] X,
  input  [3:0] Y,
  output [3:0] S,
  output C
);

  wire sum_1_c, sum_2_c, sum_3_c;

  SUM sum_1 (.X(1'b0), .Y(X[0]), .Z(Y[0]), .S(S[0]), .C(sum_1_c));
  SUM sum_2 (.X(sum_1_c), .Y(X[1]), .Z(Y[1]), .S(S[1]), .C(sum_2_c));
  SUM sum_3 (.X(sum_2_c), .Y(X[2]), .Z(Y[2]), .S(S[2]), .C(sum_3_c));
  SUM sum_4 (.X(sum_3_c), .Y(X[3]), .Z(Y[3]), .S(S[3]), .C(C));

  // Notes on the sheet:
  //   // Бит переноса
endmodule

module SUM (
  input  X,
  input  Y,
  input  Z,
  output S,
  output C
);

  wire and_1_out, and_2_out, xor_1_out;

  xor xor_1 (xor_1_out, X, Y);
  and and_1 (and_1_out, xor_1_out, Z);
  and and_2 (and_2_out, X, Y);
  xor xor_2 (S, xor_1_out, Z);
  or or_1 (C, and_1_out, and_2_out);
endmodule

module quad_memory (
  input  [3:0] IDATA,
  input  SET,
  output [3:0] ODATA
);

  D_trigger d_trigger_1 (.D(IDATA[0]), .C(SET), .Q(ODATA[0]));
  D_trigger d_trigger_2 (.D(IDATA[1]), .C(SET), .Q(ODATA[1]));
  D_trigger d_trigger_3 (.D(IDATA[2]), .C(SET), .Q(ODATA[2]));
  D_trigger d_trigger_4 (.D(IDATA[3]), .C(SET), .Q(ODATA[3]));
endmodule

module quad_memory_back (
  input  [3:0] IDATA,
  input  SET,
  output [3:0] ODATA
);

  D_trigger_back d_trigger_back_1 (.D(IDATA[0]), .C(SET), .Q(ODATA[0]));
  D_trigger_back d_trigger_back_2 (.D(IDATA[1]), .C(SET), .Q(ODATA[1]));
  D_trigger_back d_trigger_back_3 (.D(IDATA[2]), .C(SET), .Q(ODATA[2]));
  D_trigger_back d_trigger_back_4 (.D(IDATA[3]), .C(SET), .Q(ODATA[3]));
endmodule

module D_trigger (
  input  D,
  input  C,
  output Q
);

  wire not_1_out, rs_trigger_1_notq;

  not not_1 (not_1_out, D);
  RS_trigger rs_trigger_1 (.R(not_1_out), .C(C), .S(D), .Q(Q), .notQ(rs_trigger_1_notq));
  // NoConnect on rs_trigger_1_notq
endmodule

module D_trigger_front (
  input  D,
  input  C,
  output Q
);

  wire not_1_out, not_2_out, rs_trigger_1_notq, rs_trigger_1_q, rs_trigger_2_notq;

  not not_1 (not_1_out, C);
  not not_2 (not_2_out, D);
  RS_trigger rs_trigger_1 (.R(D), .C(not_1_out), .S(not_2_out), .Q(rs_trigger_1_q), .notQ(rs_trigger_1_notq));
  RS_trigger rs_trigger_2 (.R(rs_trigger_1_q), .C(C), .S(rs_trigger_1_notq), .Q(Q), .notQ(rs_trigger_2_notq));
  // NoConnect on rs_trigger_2_notq
endmodule

module D_trigger_back (
  input  D,
  input  C,
  output Q
);

  wire not_1_out;

  not not_1 (not_1_out, C);
  D_trigger_front d_trigger_front_1 (.D(D), .C(not_1_out), .Q(Q));
endmodule

module RS_trigger (
  input  R,
  input  C,
  input  S,
  output Q,
  output notQ
);

  wire and_1_out, and_2_out, or_1_out, por_1_out;

  and and_1 (and_1_out, R, C);
  and and_2 (and_2_out, C, S);
  POR #(.PorHighDuration(1)) por_1 (.out(por_1_out));
  or or_1 (or_1_out, and_2_out, por_1_out);
  nor nor_1 (Q, and_1_out, notQ);
  nor nor_2 (notQ, Q, or_1_out);
endmodule

module DEMUX_3_to_8 (
  input  D,
  input  [3:0] S,
  output i0,
  output i1,
  output i2,
  output i3,
  output i4,
  output i5,
  output i6,
  output i7
);

  and and_1 (i0, D, ~S[0], ~S[1], ~S[2]);  // AND_Gate
  and and_2 (i1, D, S[0], ~S[1], ~S[2]);  // AND_Gate
  and and_3 (i2, D, ~S[0], S[1], ~S[2]);  // AND_Gate
  and and_4 (i3, D, S[0], S[1], ~S[2]);  // AND_Gate
  and and_5 (i4, D, ~S[0], ~S[1], S[2]);  // AND_Gate
  and and_6 (i5, D, S[0], ~S[1], S[2]);  // AND_Gate
  and and_7 (i6, D, ~S[0], S[1], S[2]);  // AND_Gate
  and and_8 (i7, D, S[0], S[1], S[2]);
endmodule

module decoder_2_to_4 (
  input  i0,
  input  i1,
  output Q0,
  output Q1,
  output Q2,
  output Q3
);

  and and_1 (Q0, ~i0, ~i1);  // AND_Gate
  and and_2 (Q1, i0, ~i1);  // AND_Gate
  and and_3 (Q2, ~i0, i1);  // AND_Gate
  and and_4 (Q3, i0, i1);
endmodule

module DDDD_AND_A (
  input  [3:0] D,
  input  A,
  output [3:0] Q
);

  assign Q = D & {4{A}};  // AND_Gate and_1, 4 bits wide
endmodule

module DATA_if_F_else_UUUU (
  input  [3:0] DATA,
  input  F,
  output [3:0] ODATA
);

  X_if_F_else_U x_if_f_else_u_1 (.F(F), .X(DATA[0]), .Y(ODATA[0]));
  X_if_F_else_U x_if_f_else_u_2 (.F(F), .X(DATA[1]), .Y(ODATA[1]));
  X_if_F_else_U x_if_f_else_u_3 (.F(F), .X(DATA[2]), .Y(ODATA[2]));
  X_if_F_else_U x_if_f_else_u_4 (.F(F), .X(DATA[3]), .Y(ODATA[3]));
endmodule

module X_if_F_else_U (
  input  F,
  input  X,
  output Y
);

  wire not_1_out;

  not not_1 (not_1_out, F);
  // Transmission_Gate transmission_1: pin names not known; wires that end beside it: X, not_1_out, F, Y
endmodule

// byte
module byte_U_to_0 (
  input  [3:0] I,
  output [3:0] O
);

  U_to_0 u_to_0_1 (.I(I[0]), .O(O[0]));
  U_to_0 u_to_0_2 (.I(I[1]), .O(O[1]));
  U_to_0 u_to_0_3 (.I(I[2]), .O(O[2]));
  U_to_0 u_to_0_4 (.I(I[3]), .O(O[3]));
endmodule

module U_to_0 (
  input  I,
  output O
);

  Pull_Resistor pull_resistor_1 (.node(I));

  assign O = I;
endmodule

module M (
  input  GET,
  input  SET,
  input  [3:0] INDEX,
  input  [3:0] IDATA,
  input  CLK,
  input  RESET,
  output [3:0] ODATA
);

  wire and_1_out, and_2_out, and_3_out, and_4_out, and_5_out, and_6_out, demux_3_to_8_1_i0,
       demux_3_to_8_1_i1, demux_3_to_8_1_i2, demux_3_to_8_1_i3, demux_3_to_8_1_i4, demux_3_to_8_2_i0,
       demux_3_to_8_2_i1, demux_3_to_8_2_i2, demux_3_to_8_2_i3, demux_3_to_8_2_i4, not_1_out, not_2_out,
       not_3_out, not_4_out, not_5_out, or_1_out, or_2_out, or_3_out, or_4_out, or_5_out, or_6_out, por_1_out;
  wire [3:0] dddd_and_a_1_q, dddd_and_a_2_q, dddd_and_a_3_q, dddd_and_a_4_q, dddd_and_a_5_q, dddd_and_a_6_q,
       dddd_and_a_7_q, dddd_and_a_8_q, dddd_and_a_9_q, dddd_and_a_10_q, or_7_out, or_8_out, or_9_out,
       or_10_out, quad_memory_1_odata, quad_memory_2_odata, quad_memory_3_odata, quad_memory_4_odata,
       quad_memory_5_odata;

  DEMUX_3_to_8 demux_3_to_8_1 (
    .S(INDEX), .D(SET), .i0(demux_3_to_8_1_i0), .i1(demux_3_to_8_1_i1), .i2(demux_3_to_8_1_i2),
    .i3(demux_3_to_8_1_i3), .i4(demux_3_to_8_1_i4));  // open: i5, i6, i7
  POR #(.PorHighDuration(1)) por_1 (.out(por_1_out));
  not not_1 (not_1_out, or_1_out);
  and and_1 (and_1_out, demux_3_to_8_1_i0, CLK);
  not not_2 (not_2_out, or_1_out);
  and and_2 (and_2_out, demux_3_to_8_1_i1, CLK);
  not not_3 (not_3_out, or_1_out);
  and and_3 (and_3_out, demux_3_to_8_1_i2, CLK);
  not not_4 (not_4_out, or_1_out);
  and and_4 (and_4_out, demux_3_to_8_1_i3, CLK);
  not not_5 (not_5_out, or_1_out);
  and and_5 (and_5_out, demux_3_to_8_1_i4, CLK);
  or or_1 (or_1_out, RESET, por_1_out);
  DDDD_AND_A dddd_and_a_1 (.D(IDATA), .A(not_1_out), .Q(dddd_and_a_1_q));
  or or_2 (or_2_out, or_1_out, and_1_out);
  DDDD_AND_A dddd_and_a_2 (.D(IDATA), .A(not_2_out), .Q(dddd_and_a_2_q));
  or or_3 (or_3_out, or_1_out, and_2_out);
  DDDD_AND_A dddd_and_a_3 (.D(IDATA), .A(not_3_out), .Q(dddd_and_a_3_q));
  or or_4 (or_4_out, or_1_out, and_3_out);
  DDDD_AND_A dddd_and_a_4 (.D(IDATA), .A(not_4_out), .Q(dddd_and_a_4_q));
  or or_5 (or_5_out, or_1_out, and_4_out);
  DDDD_AND_A dddd_and_a_5 (.D(IDATA), .A(not_5_out), .Q(dddd_and_a_5_q));
  or or_6 (or_6_out, or_1_out, and_5_out);
  DEMUX_3_to_8 demux_3_to_8_2 (
    .S(INDEX), .D(GET), .i0(demux_3_to_8_2_i0), .i1(demux_3_to_8_2_i1), .i2(demux_3_to_8_2_i2),
    .i3(demux_3_to_8_2_i3), .i4(demux_3_to_8_2_i4));  // open: i5, i6, i7
  // Probe on quad_memory_1_odata
  quad_memory quad_memory_1 (.IDATA(dddd_and_a_1_q), .SET(or_2_out), .ODATA(quad_memory_1_odata));
  quad_memory quad_memory_2 (.IDATA(dddd_and_a_2_q), .SET(or_3_out), .ODATA(quad_memory_2_odata));
  // Probe on quad_memory_3_odata
  quad_memory quad_memory_3 (.IDATA(dddd_and_a_3_q), .SET(or_4_out), .ODATA(quad_memory_3_odata));
  // Probe on quad_memory_4_odata
  quad_memory quad_memory_4 (.IDATA(dddd_and_a_4_q), .SET(or_5_out), .ODATA(quad_memory_4_odata));
  // Probe on quad_memory_5_odata
  quad_memory quad_memory_5 (.IDATA(dddd_and_a_5_q), .SET(or_6_out), .ODATA(quad_memory_5_odata));
  DDDD_AND_A dddd_and_a_6 (.D(quad_memory_1_odata), .A(demux_3_to_8_2_i0), .Q(dddd_and_a_6_q));
  assign or_7_out = dddd_and_a_6_q | dddd_and_a_7_q;  // OR_Gate or_7, 4 bits wide
  DDDD_AND_A dddd_and_a_7 (.D(quad_memory_2_odata), .A(demux_3_to_8_2_i1), .Q(dddd_and_a_7_q));
  DDDD_AND_A dddd_and_a_8 (.D(quad_memory_3_odata), .A(demux_3_to_8_2_i2), .Q(dddd_and_a_8_q));
  assign or_8_out = dddd_and_a_8_q | dddd_and_a_9_q;  // OR_Gate or_8, 4 bits wide
  DDDD_AND_A dddd_and_a_9 (.D(quad_memory_4_odata), .A(demux_3_to_8_2_i3), .Q(dddd_and_a_9_q));
  DDDD_AND_A dddd_and_a_10 (.D(quad_memory_5_odata), .A(demux_3_to_8_2_i4), .Q(dddd_and_a_10_q));
  assign or_9_out = or_7_out | or_8_out;  // OR_Gate or_9, 4 bits wide
  assign or_10_out = or_9_out | dddd_and_a_10_q;  // OR_Gate or_10, 4 bits wide
  and and_6 (and_6_out, GET, CLK);
  DATA_if_F_else_UUUU data_if_f_else_uuuu_1 (.F(and_6_out), .DATA(or_10_out), .ODATA(ODATA));
endmodule
